# Fritzing sketch schematic_project (saved by Fritzing 0.9.3b)

parts:
  Part1 = Arduino Nano (Rev3.0)
  S1 = Pushbutton [package="[THT]"]
  R1 = Rotary Potentiometer (Small) [maximum_resistance=100kΩ package=THT]
  J1 = Basic Servo
  Power_plug1 = Power plug
  Display1 = LCD screen 16x2 IIC [part_number=101290]
  J2 = male pin header, 3 pins [form="♂ (male)"]

nets:
  GND: Part1.GND, S1.Pin_3, S1.Pin_4, J1.gnd, Power_plug1.GND, J2.pin1
  N1: Part1.D4, S1.Pin_2
  N2: Part1.D9, Display1.SDA
  N3: Part1.D10, Display1.SCL
  VCC: Part1.VIN, J1.vcc, Power_plug1.VCC, J2.pin2
  N4: Part1.5V, R1.leg1
  N5: Part1.A7, R1.wiper
  N6: Part1.A2, J1.pulse, J2.pin3

custom parts:
  LCD screen 16x2 IIC: LCD screen with HD44780 controller enables showing text, symbols, value or anything else that comes from Croduino/Arduino. It is capable of showing 16 symbols in two lines and therefore can be used in many projects that need to send clearly visible and legible output information.. • Color of symbols: White • Backlight: Blue • Dimensions: 80 x 36 x 12 mm • Screen dimensions: 64.5 x 16 mm •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
